// Logisim project gigatron.circ as structural Verilog: 1 circuit, main circuit main
module main (
  input  in_1,
  input  in_2,
  input  in_3,
  input  in_4
);

  wire AE_R, BUS0, BUS1, BUS2, BUS3, BUS4, BUS5, BUS6, BUS7, CLK1, CLK2, counter_1_carry, counter_2_carry,
       counter_3_carry, D0, D1, D2, D3, D4, D5, D6, D7, DE_R, decoder_2_out6, decoder_2_out7, decoder_3_out0,
       decoder_3_out1, decoder_3_out2, decoder_3_out3, decoder_3_out6, decoder_3_out7, EH, EL, IE_R, IR0,
       IR1, IR2, IR3, IR4, IR5, IR6, IR7, IX, LD, not_1_out, OE_R, OL, or_2_out, or_3_out, PC0, PC1, PC2,
       PC3, PC4, PC5, PC6, PC7, PC8, PC9, PC10, PC11, PC12, PC13, PC14, PC15, PH_R, PL_R, RST, WE, XL, Y0,
       Y1, Y2, Y3, Y4, Y5, Y6, Y7, YL;
  wire [2:2] undriven;
  wire [15:0] rom_1_data;

  Clock clock_1 (.out(CLK1));
  Button button_1 (.out(RST));
  Decoder #(.select(2)) decoder_1 (.out0(DE_R), .out1(OE_R), .out2(AE_R), .out3(IE_R), .sel({IR1, IR0}), .en(in_4));
  Decoder #(.select(3)) decoder_2 (
    .out6(decoder_2_out6), .out7(decoder_2_out7), .sel({IR7, IR6, IR5}));  // open: out0, out1, out2, out3, out4, out5, en
  buf buffer_1 (CLK2, CLK1);
  Counter #(.max('hf), .width(4)) counter_1 (
    .clr(RST), .load(PL_R), .up(in_1), .count(in_1), .clk(CLK1), .D({BUS3, undriven[2], BUS1, BUS0}),
    .carry(counter_1_carry), .Q({PC3, PC2, PC1, PC0}));
  Decoder #(.select(3)) decoder_3 (
    .out0(decoder_3_out0), .out1(decoder_3_out1), .out2(decoder_3_out2), .out3(decoder_3_out3), .out4(XL),
    .out5(YL), .out6(decoder_3_out6), .out7(decoder_3_out7), .sel({IR4, IR3, IR2}), .en(decoder_2_out7));
  ROM #(.addrWidth(16), .dataWidth(16)) rom_1 (
    .addr({PC15, PC14, PC13, PC12, PC11, PC10, PC9, PC8, PC7, PC6, PC5, PC4, PC3, PC2, PC1, PC0}),
    .data(rom_1_data));
  or or_1 (WE, decoder_2_out6, CLK1);
  not not_1 (not_1_out, decoder_2_out6);
  or or_2 (or_2_out, decoder_3_out0, decoder_3_out1, decoder_3_out2, decoder_3_out3);
  or or_3 (or_3_out, decoder_3_out6, decoder_3_out7);
  Counter #(.max('hf), .width(4)) counter_2 (
    .clr(RST), .load(PL_R), .up(in_2), .count(counter_1_carry), .clk(CLK1), .D({BUS7, BUS6, BUS5, BUS4}),
    .carry(counter_2_carry), .Q({PC7, PC6, PC5, PC4}));
  or or_4 (OL, or_3_out, not_1_out);
  or or_5 (LD, or_2_out, not_1_out);
  Register register_1 (
    .D(rom_1_data[7:0]), .en(in_3), .clk(CLK1), .Q({IR7, IR6, IR5, IR4, IR3, IR2, IR1, IR0}));  // open: clr
  Register register_2 (.D(rom_1_data[15:8]), .en(in_3), .clk(CLK1), .Q({D7, D6, D5, D4, D3, D2, D1, D0}));  // open: clr
  not not_2 (IX, decoder_3_out7);
  or or_6 (EH, decoder_3_out2, decoder_3_out3, decoder_3_out7);
  or or_7 (EL, decoder_3_out1, decoder_3_out3, decoder_3_out7);
  assign {BUS7, BUS6, BUS5, BUS4, BUS3, BUS2, BUS1, BUS0} = DE_R ? {D7, D6, D5, D4, D3, D2, D1, D0} : 8'bz;  // Controlled_Buffer controlled_buffer_1
  Counter #(.max('hf), .width(4)) counter_3 (
    .clr(RST), .load(PH_R), .up(PL_R), .count(counter_2_carry), .clk(CLK1), .D({Y3, Y2, Y1, Y0}),
    .carry(counter_3_carry), .Q({PC11, PC10, PC9, PC8}));
  Counter #(.max('hf), .width(4)) counter_4 (
    .clr(RST), .load(PH_R), .up(PL_R), .count(counter_3_carry), .clk(CLK1), .D({Y7, Y6, Y5, Y4}),
    .Q({PC15, PC14, PC13, PC12}));  // open: carry

  // Notes on the sheet:
  //   in_2: initial=0x1
  //   in_3: initial=0x1
  //   in_4: initial=0x1
  //   in_1: initial=0x1
  //   命令デコーダ
  //   BUS_ACCESS_DECODER
  //   MODE_DECODER
  //   クロック回路
  //   リセット回路
  //   ROM
  //   INSTRUCTION_DECODER
  //   プログラムカウンタ
  //   contents of rom_1 (hex, n*v repeats v):
  //   0 1880 18c0 c17f c17c 1 d601 ff 6900 ca00 c200 6900 ec0c ff 6900 ca00 6100 f015 101 fc06 8200 ff
  //   c200 ec17 a001 100 ec16 a001 1 1880 18c0 0 d218 d619 106 f426 8d00 60bf c206 107 f42b 8106 60c1 c207
  //   8108 c208 118 8001 ec22 d218 119 8001 ec22 d619 3 1880 18c0 ee c216 9002 1 d617 dc59 dc5f dc2b dc22
  //   dcb4 dce2 dc00 dc00 dcfc dc00 2 c205 ff c20e c20f c210 c211 c212 7 1880 18c0 0 c200 c202 c22c f 1880
  //   18c0 c213 c214 1401 e003 c22e 48 c221 0 c21c 1401 caf9 caf6 caf7 c22c c21a 2 c21b f6 c20a c20b c20c
  //   ad c222 bd c224 f3 c225 116 a002 c216 c17f c17c 11d 1403 e0cb e8 200 200 1403 e0cb f6 1403 e0cb f6
  //   1403 e0cb f6 1403 e0cb f6 1403 e0cb f6 1403 e0cb f6 1403 e0cb f6 1403 e0cb f6 1403 e0cb f6 1403 e0cb
  //   f6 1414 e05c 12a 1414 e094 128 1403 e0cb f6 1403 e0cb f6 1403 e0cb f6 1412 e042 0 1403 e0cb f6 1403
  //   e0cb f6 1403 e0cb f6 1403 e0cb f6 1403 e0cb f6 1403 e0cb f6 1403 e0cb f6 1403 e0cb f6 1403 e0cb f6
  //   1403 e0cb f6 1403 e0cb f6 1403 e0cb f6 1403 e0cb f6 1403 e0cb f6 1403 e0cb f6 1403 e0cb f6 1403 e0cb
  //   f6 1414 e027 119 1414 e000 1525 1413 e000 118 1413 e078 119 14f7 e06c 119 200 200 1924 200 1403 e0cb
  //   f5 c318 0 c219 200 1403 e0cb f4 1505 e0ff 7f c0 c21f 80 c220 b3 c209 1 c280 810e c20e 6107 610f 8106
  //   c206 8108 c208 e816 fc17 6053 606c 8107 c207 12d f01d fc1e a001 12f c22d f022 fc23 0 1 812e ec27
  //   fc28 e8 e42c c22e 8048 fe00 fc48 f c22e fc48 2114 f 7 3 1 2 4 8 4 2 1 3 7 f e c 8 4 2 1 2 4 8 c e
  //   c214 10 c20d 10e f052 55 c21e 1505 e0ff 23 1412 e000 1401 121 20fb c221 12c ec5c fc5d 0 f0 4114 c214
  //   12c f063 fc64 a001 0 c22c 191f 102 2121 8001 1920 d602 7f 29fe 89fc cafe 3080 500 89ff 89fd caff
  //   20fc 69fb 1200 9fa 1407 8d00 e87d fc7e 203f 3f 8103 c203 113 1412 191f 109 f4b1 8002 c209 a0bd ec8d
  //   a10d 40 fc92 c21f ec91 c0 fc93 c21f 11f 200 6040 c220 109 60cf ec9a fc9b c30f c000 109 2006 f0a6 103
  //   a4 c21e 1505 e0ff 35 fc66 191f 400f 2114 c213 c003 af c21e 1505 e0ff 33 fc66 191f e025 1401 111 60ef
  //   ecbe 112 a001 c212 207f f0c6 ee fcc5 fcc4 1 ecbf a001 200 80 c212 fccb 200 c216 1 c217 2 c205 111
  //   60df ece2 10b e8d5 10a c20b 10c c20a fcda f6 a c20b c20a 200 c20c 35 ecdc a001 200 c211 fcea 0 102
  //   2003 c202 ea c21e 1505 e0ff 26 1401 9f9 c209 c21f ecf1 fcf2 1 ec c20d 102 2121 8001 1402 e0b1 1880
  //   6*200 fcae 102 ca c20d 1401 1109 d00 de00 c220 d00 911f 1520 c0 160*5d00 18c0 102 2121 8001 1880
  //   d602 7f 29fe 89fc cafe 3080 500 89ff 89fd caff 20fc 69fb 1200 9fa 1407 8d00 e8c4 fcc5 203f 3f 8103
  //   c203 113 fd0d 18c0 d3 c20d 1401 109 9001 11f 8d00 fd0a d21f dc c20d 103 400f 2114 c213 c003 fd0b
  //   111f 111f 109 a0ee f0e5 80f0 c209 1 fd0c c20d c003 e9 fd0c c20d 1401 e004 c0 120 8080 d220 11f a500
  //   f0f4 c21f fcf6 1 c20d ff c21e 1505 e0ff 3c 4*200 fc03 1517 8115 e80b c215 116 8002 d216 d00 de00
  //   fe00 d00 800e e40c a001 1401 e11e 0 c218 de00 d00 c219 116 8001 c216 f6 fc01 1200 500 1404 e013 c218
  //   140b e0d2 1200 8001 c21d 500 c218 111d 500 c219 fc01 f6 1200 8001 c21d 118 c600 111d 119 c600 fc01
  //   f6 119 ec40 c21d 118 f043 1 c21d d00 fe00 11d ec45 f048 d00 200 fc3d d00 116 fc4a 8001 de00 d00 c216
  //   fc01 f2 f845 e448 d00 f445 e848 d00 e845 f448 d00 e445 f848 d00 c218 0 c219 fc00 f8 1200 118 c600
  //   fc00 f8 111c 500 c21a 11c 9001 500 c21b 11c 8002 c21c 116 a001 c216 fc00 f3 f045 ec48 d00 11c b001
  //   11b c600 11c a002 d21c 11a fc6d c600 1519 e0fb 8118 1404 e011 2118 140b e0c6 116 4118 c218 fc01 f9
  //   6118 c218 fc01 f9 c216 fc00 f9 1200 1404 e0e4 1 140b e0de 1200 8001 c21d 118 8500 c218 e8a3 a500
  //   fca5 4500 2500 200 3080 500 8119 111d 8500 c219 fc01 f2 1404 e062 116 a002 c216 fccb f6 8115 e8af
  //   1523 e122 1200 8001 c21d 118 e8c1 a500 c218 fcc4 4500 c218 2500 200 3080 119 a500 111d a500 c219 f2
  //   fc01 1517 1404 e007 c21d 116 8002 c21a 117 c21b 111d 500 a002 c216 11d 9001 500 d617 fc01 f3 811c
  //   c21c fc01 f9 1404 e018 c21d 1404 e026 c21d 1404 e035 118 1404 e041 1404 e04c 1404 e057 c21d 1404
  //   e06d c21d 1404 e07a 1404 e086 1404 e091 1404 e09c c21d 11a a002 c216 11b c217 1403 e0cb f6 116 8002
  //   c218 117 c219 11d c216 1403 e000 f4 200 c218 0 c219 1403 e0cb f5 8118 c218 e81e a11d fc20 411d 211d
  //   200 3080 500 8119 1403 e0ca c21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
  //   To RAM
  //   InstructionRegister
  //   DataRegister
  //   To User Registers
  //   To memory address unit
  //   To user registeres
  //   To program counter
endmodule
